// Logisim project lab1.circ as structural Verilog: 1 circuit, main circuit main
module main (
  input  in_1,
  input  in_2,
  input  in_3,
  input  in_4,
  input  in_5,
  input  in_6,
  input  in_7,
  input  in_8,
  input  in_9,
  input  in_10
);

  wire and_1_out, and_2_out, not_1_out, not_2_out, xnor_1_out, xnor_2_out, xor_1_out, xor_2_out;

  and and_1 (and_1_out, in_2, in_7);
  LED led_1 (.in(and_1_out));
  not not_1 (not_1_out, in_5);
  LED led_2 (.in(not_1_out));
  xor xor_1 (xor_1_out, in_3, in_8);
  LED led_3 (.in(xor_1_out));
  xor xor_2 (xor_2_out, in_4, in_9);
  not not_2 (not_2_out, xor_2_out);
  LED led_4 (.in(not_2_out));
  xnor xnor_1 (xnor_1_out, in_1, in_6);
  xnor xnor_2 (xnor_2_out, in_6, in_10);
  and and_2 (and_2_out, xnor_1_out, xnor_2_out);
  LED led_5 (.in(and_2_out));

  // Notes on the sheet:
  //   And gate
  //   XOR gate
  //   NOT gate
  //   XNOR Gate
  //   XNOR Gate
  //   AND Gate
endmodule
