// Logisim project lab2.circ as structural Verilog: 1 circuit, main circuit main
module main (
  input  in_1,
  input  in_2,
  input  in_3,
  input  in_4,
  input  in_5,
  input  in_6,
  input  in_7,
  input  in_8,
  input  in_9,
  input  in_10,
  input  in_11,
  input  in_12,
  input  in_13,
  input  in_14
);

  wire and_1_out, and_2_out, and_3_out, and_4_out, and_5_out, and_6_out, and_7_out, and_8_out, and_9_out,
       and_10_out, or_1_out, or_2_out, or_3_out, or_4_out, xor_1_out, xor_2_out, xor_3_out, xor_4_out,
       xor_5_out, xor_6_out, xor_7_out, xor_8_out, xor_9_out, xor_10_out;

  xor xor_1 (xor_1_out, in_8, in_1);
  and and_1 (and_1_out, in_8, in_1);
  LED led_1 (.in(xor_1_out));
  LED led_2 (.in(and_1_out));
  and and_2 (and_2_out, in_9, in_3);
  and and_3 (and_3_out, in_2, xor_2_out);
  or or_1 (or_1_out, and_3_out, and_2_out);
  LED led_3 (.in(or_1_out));
  xor xor_2 (xor_2_out, in_9, in_3);
  xor xor_3 (xor_3_out, in_2, xor_2_out);
  LED led_4 (.in(xor_3_out));
  and and_4 (and_4_out, in_10, in_4);
  or or_2 (or_2_out, and_4_out, and_5_out);
  xor xor_4 (xor_4_out, in_10, in_4);
  xor xor_5 (xor_5_out, xor_4_out, or_3_out);
  and and_5 (and_5_out, xor_4_out, or_3_out);
  LED led_5 (.in(xor_5_out));
  and and_6 (and_6_out, in_11, in_5);
  and and_7 (and_7_out, xor_6_out, or_4_out);
  or or_3 (or_3_out, and_6_out, and_7_out);
  xor xor_6 (xor_6_out, in_11, in_5);
  xor xor_7 (xor_7_out, xor_6_out, or_4_out);
  LED led_6 (.in(xor_7_out));
  and and_8 (and_8_out, in_12, in_6);
  xor xor_8 (xor_8_out, in_12, in_6);
  and and_9 (and_9_out, xor_8_out, and_10_out);
  or or_4 (or_4_out, and_8_out, and_9_out);
  xor xor_9 (xor_9_out, xor_8_out, and_10_out);
  LED led_7 (.in(xor_9_out));
  and and_10 (and_10_out, in_13, in_7);
  xor xor_10 (xor_10_out, in_13, in_7);
  LED led_8 (.in(xor_10_out));

  // Notes on the sheet:
  //   HALF ADDER
  //   FULL ADDER
  //   2 power 3
  //   2 power 2
  //   2 power 1
  //   2 power 0
endmodule
