// Logisim project lab3.circ as structural Verilog: 1 circuit, main circuit main
module main (
  input  SET,
  input  in_2,
  input  in_3,
  input  in_4,
  input  in_5,
  input  RESET,
  input  in_7,
  input  in_8,
  input  J,
  input  K
);

  wire and_1_out, and_2_out, clock_1_out, clock_2_out, clock_3_out, d_ff_1_q, d_ff_2_q, d_ff_3_q, d_ff_4_q,
       nand_1_out, nand_2_out, nand_3_out, nand_4_out, nor_1_out, nor_2_out, nor_3_out, nor_4_out, not_1_out;

  Clock clock_1 (.out(clock_1_out));
  Clock clock_2 (.out(clock_2_out));
  not not_1 (not_1_out, in_8);
  nand nand_1 (nand_1_out, nand_4_out, J, clock_2_out);
  nand nand_2 (nand_2_out, clock_2_out, K, nand_3_out);
  and and_1 (and_1_out, clock_1_out, not_1_out);
  and and_2 (and_2_out, clock_1_out, in_8);
  nor nor_1 (nor_1_out, SET, nor_2_out);
  nor nor_2 (nor_2_out, nor_1_out, RESET);
  LED led_1 (.in(nor_2_out));
  nor nor_3 (nor_3_out, and_1_out, nor_4_out);
  nor nor_4 (nor_4_out, nor_3_out, and_2_out);
  nand nand_3 (nand_3_out, nand_1_out, nand_4_out);
  nand nand_4 (nand_4_out, nand_3_out, nand_2_out);
  LED led_2 (.in(nor_1_out));
  LED led_3 (.in(nor_3_out));
  LED led_4 (.in(nor_4_out));
  LED led_5 (.in(nand_3_out));
  LED led_6 (.in(nand_4_out));
  Clock clock_3 (.out(clock_3_out));
  D_Flip_Flop d_ff_1 (.D(in_2), .clk(clock_3_out), .Q(d_ff_1_q), .reset(in_7));  // open: Qn, preset
  LED led_7 (.in(d_ff_1_q));
  D_Flip_Flop d_ff_2 (.D(in_3), .clk(clock_3_out), .Q(d_ff_2_q), .reset(in_7));  // open: Qn, preset
  LED led_8 (.in(d_ff_2_q));
  D_Flip_Flop d_ff_3 (.D(in_4), .clk(clock_3_out), .Q(d_ff_3_q), .reset(in_7));  // open: Qn, preset
  LED led_9 (.in(d_ff_3_q));
  D_Flip_Flop d_ff_4 (.D(in_5), .clk(clock_3_out), .Q(d_ff_4_q), .reset(in_7));  // open: Qn, preset
  LED led_10 (.in(d_ff_4_q));

  // Notes on the sheet:
  //   PART 1
  //   Q
  //   Q'
  //   Q
  //   Q'
  //   PART 2
endmodule
