// Logisim project lab4.circ as structural Verilog: 1 circuit, main circuit main
module main (
  input  in_1,
  input  in_2,
  input  in_3,
  input  in_4,
  input  in_5,
  input  in_6,
  input  in_7
);

  wire and_1_out, and_2_out, and_3_out, and_4_out, and_5_out, and_6_out, clock_1_out, clock_2_out,
       clock_3_out, clock_4_out, clock_5_out, clock_6_out, j_k_ff_1_q, j_k_ff_2_q, j_k_ff_3_q, j_k_ff_4_q,
       j_k_ff_5_q, j_k_ff_6_q, j_k_ff_7_q, j_k_ff_8_q, j_k_ff_9_q, j_k_ff_10_q, j_k_ff_11_q, j_k_ff_12_q,
       j_k_ff_13_q, j_k_ff_14_q, j_k_ff_15_q, j_k_ff_16_q, j_k_ff_17_q, j_k_ff_18_q;
  wire [3:1] d_ff_3_q;

  J_K_Flip_Flop #(.trigger("falling")) j_k_ff_1 (
    .J(in_3), .K(in_3), .clk(j_k_ff_3_q), .Q(j_k_ff_1_q));  // open: Qn, preset, reset
  J_K_Flip_Flop j_k_ff_2 (.J(in_6), .K(in_6), .clk(j_k_ff_4_q), .Q(j_k_ff_2_q));  // open: Qn, preset, reset
  LED led_1 (.in(j_k_ff_1_q));
  LED led_2 (.in(j_k_ff_2_q));
  J_K_Flip_Flop #(.trigger("falling")) j_k_ff_3 (
    .J(in_3), .K(in_3), .clk(j_k_ff_5_q), .Q(j_k_ff_3_q));  // open: Qn, preset, reset
  J_K_Flip_Flop j_k_ff_4 (.J(in_6), .K(in_6), .clk(j_k_ff_6_q), .Q(j_k_ff_4_q));  // open: Qn, preset, reset
  LED led_3 (.in(j_k_ff_3_q));
  LED led_4 (.in(j_k_ff_4_q));
  J_K_Flip_Flop #(.trigger("falling")) j_k_ff_5 (
    .J(in_3), .K(in_3), .clk(clock_1_out), .Q(j_k_ff_5_q));  // open: Qn, preset, reset
  J_K_Flip_Flop j_k_ff_6 (.J(in_6), .K(in_6), .clk(clock_2_out), .Q(j_k_ff_6_q));  // open: Qn, preset, reset
  LED led_5 (.in(j_k_ff_5_q));
  Clock clock_1 (.out(clock_1_out));
  LED led_6 (.in(j_k_ff_6_q));
  Clock clock_2 (.out(clock_2_out));
  Clock clock_3 (.out(clock_3_out));
  Clock clock_4 (.out(clock_4_out));
  J_K_Flip_Flop j_k_ff_7 (.J(and_3_out), .K(and_3_out), .clk(clock_5_out), .Q(j_k_ff_7_q));  // open: Qn, preset, reset
  Clock clock_5 (.out(clock_5_out));
  J_K_Flip_Flop j_k_ff_8 (.J(and_1_out), .K(and_1_out), .clk(clock_3_out), .Q(j_k_ff_8_q));  // open: Qn, preset, reset
  J_K_Flip_Flop j_k_ff_9 (.J(and_2_out), .K(and_2_out), .clk(clock_4_out), .Q(j_k_ff_9_q));  // open: Qn, preset, reset
  LED led_7 (.in(j_k_ff_7_q));
  LED led_8 (.in(j_k_ff_8_q));
  and and_1 (and_1_out, j_k_ff_10_q, j_k_ff_14_q);
  LED led_9 (.in(j_k_ff_9_q));
  and and_2 (and_2_out, j_k_ff_11_q, j_k_ff_15_q);
  and and_3 (and_3_out, j_k_ff_12_q, j_k_ff_13_q);
  J_K_Flip_Flop j_k_ff_10 (
    .J(j_k_ff_14_q), .K(j_k_ff_14_q), .clk(clock_3_out), .Q(j_k_ff_10_q), .reset(and_4_out));  // open: Qn, preset
  and and_4 (and_4_out, j_k_ff_8_q, j_k_ff_10_q, j_k_ff_14_q);
  J_K_Flip_Flop j_k_ff_11 (
    .J(j_k_ff_15_q), .K(j_k_ff_15_q), .clk(clock_4_out), .Q(j_k_ff_11_q), .reset(and_5_out));  // open: Qn, preset
  and and_5 (and_5_out, j_k_ff_9_q, j_k_ff_11_q);
  J_K_Flip_Flop j_k_ff_12 (
    .J(j_k_ff_13_q), .K(j_k_ff_13_q), .clk(clock_5_out), .Q(j_k_ff_12_q));  // open: Qn, preset, reset
  LED led_10 (.in(j_k_ff_10_q));
  LED led_11 (.in(j_k_ff_11_q));
  LED led_12 (.in(j_k_ff_12_q));
  J_K_Flip_Flop j_k_ff_13 (.J(in_1), .K(in_1), .clk(clock_5_out), .Q(j_k_ff_13_q));  // open: Qn, preset, reset
  J_K_Flip_Flop j_k_ff_14 (.J(in_5), .K(in_5), .clk(clock_3_out), .Q(j_k_ff_14_q));  // open: Qn, preset, reset
  LED led_13 (.in(j_k_ff_15_q));
  J_K_Flip_Flop j_k_ff_15 (.J(in_7), .K(in_7), .clk(clock_4_out), .Q(j_k_ff_15_q));  // open: Qn, preset, reset
  LED led_14 (.in(j_k_ff_13_q));
  LED led_15 (.in(j_k_ff_14_q));
  Clock clock_6 (.out(clock_6_out));
  J_K_Flip_Flop j_k_ff_16 (
    .J(and_6_out), .K(and_6_out), .clk(clock_6_out), .Q(j_k_ff_16_q));  // open: Qn, preset, reset
  D_Flip_Flop d_ff_1 (.D(j_k_ff_16_q), .clk(clock_6_out), .Q(d_ff_3_q[3]));  // open: Qn, preset, reset
  and and_6 (and_6_out, j_k_ff_17_q, j_k_ff_18_q);
  J_K_Flip_Flop j_k_ff_17 (
    .J(j_k_ff_18_q), .K(j_k_ff_18_q), .clk(clock_6_out), .Q(j_k_ff_17_q));  // open: Qn, preset, reset
  D_Flip_Flop d_ff_2 (.D(j_k_ff_17_q), .clk(clock_6_out), .Q(d_ff_3_q[2]));  // open: Qn, preset, reset
  J_K_Flip_Flop j_k_ff_18 (.J(in_4), .K(in_4), .clk(clock_6_out), .Q(j_k_ff_18_q));  // open: Qn, preset, reset
  D_Flip_Flop d_ff_3 (.D(j_k_ff_18_q), .clk(clock_6_out), .Q(d_ff_3_q[1]), .preset(d_ff_3_q[2]));  // open: Qn, reset
  Hex_Digit_Display hex_digit_display_1 (.value({d_ff_3_q, in_2}));  // open: dp
endmodule
