// Logisim project lab5.circ as structural Verilog: 1 circuit, main circuit main
module main (
  input  in_1,
  input  in_2,
  input  in_3,
  input  in_4,
  input  in_5,
  input  in_6,
  input  in_7,
  input  in_8,
  input  in_9,
  input  in_10
);

  wire and_1_out, and_2_out, and_3_out, and_4_out, and_5_out, and_6_out, and_7_out, and_8_out, and_9_out,
       and_10_out, and_11_out, and_12_out, and_13_out, and_14_out, and_15_out, and_16_out, and_17_out,
       and_18_out, and_19_out, and_20_out, and_21_out, and_22_out, and_23_out, and_24_out, and_25_out,
       and_26_out, clock_1_out, d_ff_1_q, d_ff_2_q, d_ff_3_q, d_ff_4_q, d_ff_5_q, d_ff_6_q, d_ff_7_q,
       d_ff_8_q, d_ff_9_q, d_ff_10_q, d_ff_11_q, d_ff_12_q, d_ff_13_q, d_ff_14_q, d_ff_15_q, not_1_out,
       not_2_out, or_1_out, or_2_out, or_3_out, or_4_out, or_5_out, or_6_out, or_7_out, or_8_out, or_9_out,
       or_10_out;

  not not_1 (not_1_out, in_1);
  and and_1 (and_1_out, in_1, in_3);
  Clock clock_1 (.out(clock_1_out));
  not not_2 (not_2_out, in_5);
  and and_2 (and_2_out, in_5, in_7);
  or or_1 (or_1_out, and_2_out, and_4_out);
  and and_3 (and_3_out, not_1_out, d_ff_4_q);
  or or_2 (or_2_out, and_1_out, and_3_out);
  D_Flip_Flop d_ff_1 (.D(or_2_out), .clk(clock_1_out), .Q(d_ff_1_q), .reset(in_4));  // open: Qn, preset
  and and_4 (and_4_out, not_2_out, d_ff_5_q);
  D_Flip_Flop d_ff_2 (.D(or_1_out), .clk(in_9), .Q(d_ff_2_q), .reset(in_8));  // open: Qn, preset
  and and_5 (and_5_out, in_9, in_10);
  LED led_1 (.in(d_ff_1_q));
  LED led_2 (.in(d_ff_2_q));
  D_Flip_Flop d_ff_3 (.D(d_ff_2_q), .clk(and_5_out), .Q(d_ff_3_q), .preset(and_10_out));  // open: Qn, reset
  and and_6 (and_6_out, in_1, d_ff_1_q);
  and and_7 (and_7_out, not_1_out, d_ff_8_q);
  or or_3 (or_3_out, and_6_out, and_7_out);
  D_Flip_Flop d_ff_4 (.D(or_3_out), .clk(clock_1_out), .Q(d_ff_4_q), .reset(in_4));  // open: Qn, preset
  and and_8 (and_8_out, in_5, d_ff_2_q);
  and and_9 (and_9_out, not_2_out, d_ff_6_q);
  or or_4 (or_4_out, and_8_out, and_9_out);
  D_Flip_Flop d_ff_5 (.D(or_4_out), .clk(in_9), .Q(d_ff_5_q), .reset(in_8));  // open: Qn, preset
  and and_10 (and_10_out, d_ff_2_q, in_9);
  LED led_3 (.in(d_ff_3_q));
  LED led_4 (.in(d_ff_4_q));
  LED led_5 (.in(d_ff_5_q));
  and and_11 (and_11_out, in_1, d_ff_4_q);
  or or_5 (or_5_out, and_11_out, and_15_out);
  and and_12 (and_12_out, in_5, d_ff_5_q);
  and and_13 (and_13_out, not_2_out, d_ff_11_q);
  or or_6 (or_6_out, and_12_out, and_13_out);
  D_Flip_Flop d_ff_6 (.D(or_6_out), .clk(in_9), .Q(d_ff_6_q), .reset(in_8));  // open: Qn, preset
  and and_14 (and_14_out, d_ff_5_q, in_9);
  D_Flip_Flop d_ff_7 (.D(d_ff_5_q), .clk(and_5_out), .Q(d_ff_7_q), .preset(and_14_out));  // open: Qn, reset
  LED led_6 (.in(d_ff_7_q));
  and and_15 (and_15_out, not_1_out, d_ff_10_q);
  D_Flip_Flop d_ff_8 (.D(or_5_out), .clk(clock_1_out), .Q(d_ff_8_q), .reset(in_4));  // open: Qn, preset
  LED led_7 (.in(d_ff_6_q));
  and and_16 (and_16_out, in_1, d_ff_8_q);
  LED led_8 (.in(d_ff_8_q));
  and and_17 (and_17_out, in_5, d_ff_6_q);
  or or_7 (or_7_out, and_17_out, and_20_out);
  and and_18 (and_18_out, d_ff_6_q, in_9);
  D_Flip_Flop d_ff_9 (.D(d_ff_6_q), .clk(and_5_out), .Q(d_ff_9_q), .preset(and_18_out));  // open: Qn, reset
  and and_19 (and_19_out, not_1_out, d_ff_13_q);
  or or_8 (or_8_out, and_16_out, and_19_out);
  D_Flip_Flop d_ff_10 (.D(or_8_out), .clk(clock_1_out), .Q(d_ff_10_q), .reset(in_4));  // open: Qn, preset
  and and_20 (and_20_out, not_2_out, d_ff_14_q);
  D_Flip_Flop d_ff_11 (.D(or_7_out), .clk(in_9), .Q(d_ff_11_q), .reset(in_8));  // open: Qn, preset
  LED led_9 (.in(d_ff_9_q));
  LED led_10 (.in(d_ff_10_q));
  LED led_11 (.in(d_ff_11_q));
  D_Flip_Flop d_ff_12 (.D(d_ff_11_q), .clk(and_5_out), .Q(d_ff_12_q), .preset(and_25_out));  // open: Qn, reset
  and and_21 (and_21_out, in_1, d_ff_10_q);
  and and_22 (and_22_out, not_1_out, in_2);
  or or_9 (or_9_out, and_21_out, and_22_out);
  D_Flip_Flop d_ff_13 (.D(or_9_out), .clk(clock_1_out), .Q(d_ff_13_q), .reset(in_4));  // open: Qn, preset
  and and_23 (and_23_out, in_5, d_ff_11_q);
  and and_24 (and_24_out, not_2_out, in_6);
  or or_10 (or_10_out, and_23_out, and_24_out);
  D_Flip_Flop d_ff_14 (.D(or_10_out), .clk(in_9), .Q(d_ff_14_q), .reset(in_8));  // open: Qn, preset
  and and_25 (and_25_out, d_ff_11_q, in_9);
  LED led_12 (.in(d_ff_12_q));
  LED led_13 (.in(d_ff_13_q));
  LED led_14 (.in(d_ff_14_q));
  and and_26 (and_26_out, d_ff_14_q, in_9);
  D_Flip_Flop d_ff_15 (.D(d_ff_14_q), .clk(and_5_out), .Q(d_ff_15_q), .preset(and_26_out));  // open: Qn, reset
  LED led_15 (.in(d_ff_15_q));
endmodule
